# Fritzing sketch Neopixel Raspberry Pi HAT v4 (saved by Fritzing 0.9.3b)
circuit board: 6.50001cm x 5.64998cm
perfboards: 1

parts:
  J2 = shrouded pin header, 40 pins [form="♂ (shrouded male)"]
  74HCT08 = 74HC08 Logic AND Gate [part_number=74HCT08 package="DIP (Dual Inline) [THT]"]
  R1 = Resistor [tolerance=±5% resistance=220 package=THT]
  J13 = double row female pin header, 6 pins [form="♀ (female)"]
  ATTINY85 = attiny85 [package=dip]
  R2 = Resistor [tolerance=±5% resistance=220 package=THT]
  J12 = double row female pin header, 16 pins [form="♀ (female)"]
  J14 = screw terminal, 2 pins
  LED1 = LED - 3mm [color="Red (633nm)" package="3 mm [THT]"]
  LED2 = LED - 3mm [color="Red (633nm)" package="3 mm [THT]"]

nets:
  N1: J2.pin2, ATTINY85.Pin_5
  N2: J2.pin3, ATTINY85.Pin_7
  N3: J2.pin9, ATTINY85.Pin_8
  N4: J2.pin20, 74HCT08.GND, J13.pin3, J13.pin4, ATTINY85.Pin_4, J12.pin9, J12.pin10, J12.pin11, J12.pin12, J12.pin13, J12.pin14, J12.pin15, J12.pin16, J14.pin2, LED1.cathode, LED2.cathode
  N5: 74HCT08.1B, 74HCT08.1Y, ATTINY85.Pin_6
  N6: 74HCT08.2A, J13.pin2, J13.pin5
  N7: 74HCT08.VCC, J13.pin1, J13.pin6, J12.pin1, J12.pin2, J12.pin3, J12.pin4, J12.pin5, J12.pin6, J12.pin7, J12.pin8, J14.pin1
  N8: R1.Pin_0, LED1.anode
  N9: R1.Pin_1, ATTINY85.Pin_2
  N10: ATTINY85.Pin_3, R2.Pin_1
  N11: R2.Pin_0, LED2.anode

notes:
  5v/GND
  5v/D0/GND
  GNDx8
  5vx8
  Output
  Input
  Neopixel Raspberry PI HAT version 4
