# Fritzing sketch Neopixel Raspberry Pi HAT v5 (saved by Fritzing 0.9.3b)
circuit board: 6.50001cm x 5.64998cm
breadboards: 1

parts:
  J2 = shrouded pin header, 40 pins [form="♂ (shrouded male)"]
  ATMEGA328 = atmega328 [package=dip]
  R5 = Resistor [tolerance=±5% resistance=220 package=THT]
  R6 = Resistor [tolerance=±5% resistance=220 package=THT]
  74HCT08 = 74HC08 Logic AND Gate [part_number=74HCT08 package="DIP (Dual Inline) [THT]"]
  5v/D0/GND = female pin header, 3 pins [form="♀ (female)"]
  R4 = Resistor [tolerance=±5% resistance=220 package=THT]
  R3 = Resistor [tolerance=±5% resistance=220 package=THT]
  Pi-5v = female pin header, 2 pins [form="♀ (female)"]
  LED3 = LED - 5mm [color="Red (633nm)" package="5 mm [THT]"]
  LED4 = LED - 5mm [color="Red (633nm)" package="5 mm [THT]"]
  LED5 = LED - 5mm [color="Red (633nm)" package="5 mm [THT]"]
  R2 = Resistor [tolerance=±5% resistance=220 package=THT]
  LED2 = LED - 5mm [color="Red (633nm)" package="5 mm [THT]"]
  R1 = Resistor [tolerance=±5% resistance=220 package=THT]
  LED1 = LED - 5mm [color="Red (633nm)" package="5 mm [THT]"]
  J16 = female pin header, 8 pins [form="♀ (female)"]  # not connected
  C1 = Electrolytic Capacitor [capacitance=4.7mF package="200 mil [THT, electrolytic]"]
  J17 = female pin header, 3 pins [form="♀ (female)"]
  5v/GND = female pin header, 2 pins [form="♀ (female)"]

nets (from the pcb view):
  N1: J2.pin2, ATMEGA328.A4
  N2: J2.pin3, ATMEGA328.A5
  N3: J2.pin9, ATMEGA328.VCC, ATMEGA328.AVCC
  GND: J2.pin20, ATMEGA328.GND, 74HCT08.GND, 5v/D0/GND.pin3, LED3.cathode, LED4.cathode, LED5.cathode, LED2.cathode, LED1.cathode, C1.-, 5v/GND.pin2
  N4: J2.pin40, 74HCT08.VCC, Pi-5v.pin1
  N5: ATMEGA328.D4, 74HCT08.1A, 74HCT08.1B, 74HCT08.2A, 74HCT08.2B, 74HCT08.3A, 74HCT08.3B, 74HCT08.4A, 74HCT08.4B
  N6: ATMEGA328.D9_(PWM), R5.Pin_0
  N7: ATMEGA328.D10_(PWM), R4.Pin_0
  N8: ATMEGA328.D11_(PWM), R3.Pin_0
  N9: ATMEGA328.D12, R2.Pin_0
  N10: ATMEGA328.D13, R1.Pin_0
  N11: R5.Pin_1, LED5.anode
  N12: R6.Pin_0, 5v/D0/GND.pin2
  N13: R6.Pin_1, 74HCT08.1Y
  N14: 5v/D0/GND.pin1, Pi-5v.pin2, C1.+, J17.pin2
  N15: R4.Pin_1, LED4.anode
  N16: R3.Pin_1, LED3.anode
  N17: R2.Pin_1, LED2.anode
  N18: R1.Pin_1, LED1.anode
  N19: J17.pin3, 5v/GND.pin1

notes:
  Neopixel Raspberry PI HAT version 5
