# Fritzing sketch Neopixel Raspberry Pi HAT v9 (saved by Fritzing 0.9.3b)
circuit board: 6.50001cm x 5.64998cm
breadboards: 1

parts:
  J2 = shrouded pin header, 40 pins [form="♂ (shrouded male)"]
  R5 = Resistor [tolerance=±5% resistance=220 package=THT]
  R4 = Resistor [tolerance=±5% resistance=220 package=THT]
  R3 = Resistor [tolerance=±5% resistance=220 package=THT]
  R2 = Resistor [tolerance=±5% resistance=220 package=THT]
  R1 = Resistor [tolerance=±5% resistance=220 package=THT]
  ATMEGA328 = atmega328 [package=dip]
  R6 = Resistor [tolerance=±5% resistance=330 package=THT]
  LED_5v/D0/GND = screw terminal, 3 pins
  LED1 = LED - 3mm [color="Red (633nm)" package="3 mm [THT]"]
  LED2 = LED - 3mm [color="Red (633nm)" package="3 mm [THT]"]
  LED5 = LED - 3mm [color="Red (633nm)" package="3 mm [THT]"]
  C1 = Electrolytic Capacitor [capacitance=1mF voltage=35V part_number="1000uF 25V 85C" package="200 mil [THT, electrolytic]"]
  USB-A = USB Connectors [package=usb-a-h]  # not connected
  LED4 = LED - 3mm [color="Red (633nm)" package="3 mm [THT]"]
  LED3 = LED - 3mm [color="Red (633nm)" package="3 mm [THT]"]
  5v/GND = screw terminal, 2 pins
  USB-A_2 = USB Connectors [package=usb-a-h]  # not connected
  S1 = Toggle Switch [package=THT]  # not connected

nets (from the breadboard view):
  N1: J2.pin2, ATMEGA328.A4
  N2: J2.pin3, ATMEGA328.A5
  N3: J2.pin20, ATMEGA328.GND, LED_5v/D0/GND.pin3, LED1.cathode, LED2.cathode, LED5.cathode, C1.-, LED4.cathode, LED3.cathode, 5v/GND.pin2
  N4: R5.Pin_0, ATMEGA328.D9_(PWM)
  N5: R5.Pin_1, LED5.anode
  N6: R4.Pin_0, ATMEGA328.D10_(PWM)
  N7: R4.Pin_1, LED4.anode
  N8: R3.Pin_0, ATMEGA328.D11_(PWM)
  N9: R3.Pin_1, LED3.anode
  N10: R2.Pin_0, ATMEGA328.D12
  N11: R2.Pin_1, LED2.anode
  N12: R1.Pin_0, ATMEGA328.D13
  N13: R1.Pin_1, LED1.anode
  N14: ATMEGA328.D4, R6.Pin_1
  N15: ATMEGA328.VCC, ATMEGA328.AVCC, LED_5v/D0/GND.pin1, C1.+, 5v/GND.pin1
  N16: R6.Pin_0, LED_5v/D0/GND.pin2

notes:
  Neopixel Raspberry PI HAT version 9
